# Fritzing sketch ボタンとLED回路 (saved by Fritzing 1.0.2b)
breadboards: 1

parts:
  R1 = Resistor [tolerance=±5% resistance=51 power=0.25W package=THT]
  LED1 = LED - 5mm [color="Yellow (595nm)" current=0.030A package="5 mm [THT]"]
  S1 = Pushbutton [package="[THT]"]
  Raspberry_Pi_1 = Raspberry Pi 3 [part_number=RPI-3-V1.2]
  FTDI_USB_UART1 = CP2102 USB UART [part_number="USB UART"]
  DS3231 = Adafruit DS3231 [part_number="Adafruit #3013"]
  電池CR1220 = DC Power [voltage=5]

nets:
  N1: R1.Pin_0, LED1.anode
  N2: R1.Pin_1, Raspberry_Pi_1.GPIO19
  GND: LED1.cathode, Raspberry_Pi_1.GND, FTDI_USB_UART1.GND, DS3231.GND, 電池CR1220.V-
  3.3V: S1.Pin_1, S1.Pin_2, Raspberry_Pi_1.3v3, Raspberry_Pi_1.3V3, FTDI_USB_UART1.3V3, DS3231.Vin
  Button: S1.Pin_3, S1.Pin_4, Raspberry_Pi_1.GPIO26
  N3: Raspberry_Pi_1.GPIO2, DS3231.SDA
  N4: Raspberry_Pi_1.GPIO3, DS3231.SCL
  N5: Raspberry_Pi_1.GPIO15, FTDI_USB_UART1.TXO
  N6: Raspberry_Pi_1.GPIO14, FTDI_USB_UART1.RXI
  N7: DS3231.BAT, 電池CR1220.V+

custom parts:
  CP2102 USB UART: CP2102 USB UART FTDI
  Adafruit DS3231: The datasheet for the DS3231 explains that this part is an "Extremely Accurate I²C-Integrated RTC/TCXO/Crystal". And, hey, it does exactly what it says on the tin! This Real Time Clock (RTC) is the most precise you can get in a small, low power package. Most RTCs use an external 32kHz timing crystal that is used to keep time with low current draw. And that's all well and good, but those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
